// Logisim project cpu.circ as structural Verilog: 7 circuits, main circuit main
module main (
  input  [3:0] in_1,
  input  [3:0] in_2
);

  wire [3:0] adder4_1_s;

  Adder4 adder4_1 (.A(in_1), .B(in_2), .S(adder4_1_s));  // open: C
  Hex_Digit_Display hex_digit_display_1 (.value(adder4_1_s));  // open: dp
endmodule

module Adder1 (
  input  A,
  input  B,
  output S,
  output C
);

  xor xor_1 (S, A, B);
  and and_1 (C, A, B);
endmodule

module Adder1C (
  input  A,
  input  B,
  input  C,
  output S,
  output C_2
);

  wire adder1_1_c, adder1_1_s, adder1_2_c;

  Adder1 adder1_1 (.A(A), .B(B), .S(adder1_1_s), .C(adder1_1_c));
  Adder1 adder1_2 (.A(adder1_1_s), .B(C), .S(S), .C(adder1_2_c));
  or or_1 (C_2, adder1_1_c, adder1_2_c);
endmodule

module Adder4 (
  input  [3:0] A,
  input  [3:0] B,
  output [3:0] S,
  output C
);

  wire adder1_1_c, adder1c_1_c_2, adder1c_2_c_2;

  Adder1 adder1_1 (.A(A[0]), .B(B[0]), .S(S[0]), .C(adder1_1_c));
  Adder1C adder1c_1 (.A(adder1_1_c), .B(A[1]), .C(B[1]), .S(S[1]), .C_2(adder1c_1_c_2));
  Adder1C adder1c_2 (.A(adder1c_1_c_2), .B(A[2]), .C(B[2]), .S(S[2]), .C_2(adder1c_2_c_2));
  Adder1C adder1c_3 (.A(adder1c_2_c_2), .B(A[3]), .C(B[3]), .S(S[3]), .C_2(C));
endmodule

module And4 (
  input  [3:0] A,
  input  [3:0] B,
  output [3:0] S
);

  and and_1 (S[0], A[0], B[0]);
  and and_2 (S[1], A[1], B[1]);
  and and_3 (S[2], A[2], B[2]);
  and and_4 (S[3], A[3], B[3]);
endmodule

module Or4 (
  input  [3:0] A,
  input  [3:0] B,
  output [3:0] S
);

  or or_1 (S[0], A[0], B[0]);
  or or_2 (S[1], A[1], B[1]);
  or or_3 (S[2], A[2], B[2]);
  or or_4 (S[3], A[3], B[3]);
endmodule

module Xor4 (
  input  [3:0] A,
  input  [3:0] B,
  output [3:0] S
);

  xor xor_1 (S[0], A[0], B[0]);
  xor xor_2 (S[1], A[1], B[1]);
  xor xor_3 (S[2], A[2], B[2]);
  xor xor_4 (S[3], A[3], B[3]);
endmodule
